# Fritzing sketch マイクロマウス用ストップウォッチの配線図 (saved by Fritzing 0.9.9b)
breadboards: 2

parts:
  7_Segment_4_Digit_Display1 = 7-SEGMENT-4DIGIT common anode [part_number="5461BS - 5462BS" package=7-segment-4digit-anode]
  ESP1 = SWITCH SCIENCE ESPr Developer 32
  R1 = Resistor [tolerance=±5% power=0.25 resistance=33k package=THT]
  R2 = Resistor [tolerance=±5% power=0.25 resistance=33k package=THT]
  R3 = Resistor [tolerance=±5% power=0.25 resistance=33k package=THT]
  R4 = Resistor [tolerance=±5% power=0.25 resistance=33k package=THT]
  BAT1 = Battery Holders [package=lipo-1100mAh]  # not connected
  Q1 = LTR-301 [package=ltr-301]
  Q2 = LTR-301 [package=ltr-301]
  LED2 = Infrared LED - 5mm [package="5 mm [THT]"]
  LED1 = Infrared LED - 5mm [package="5 mm [THT]"]
  R5 = Resistor [tolerance=±5% power=0.25 resistance=220 package=THT]
  R6 = Resistor [tolerance=±5% power=0.25 resistance=220 package=THT]
  R7 = Resistor [tolerance=±5% power=0.25 resistance=220 package=THT]
  R8 = Resistor [tolerance=±5% power=0.25 resistance=220 package=THT]

nets:
  N1: 7_Segment_4_Digit_Display1.pin_1, ESP1.io4
  N2: 7_Segment_4_Digit_Display1.pin_2, ESP1.io21
  N3: 7_Segment_4_Digit_Display1.pin_3, ESP1.io19
  N4: 7_Segment_4_Digit_Display1.pin_4, ESP1.io18
  N5: 7_Segment_4_Digit_Display1.pin_5, ESP1.io5
  N6: 7_Segment_4_Digit_Display1.pin_6, R4.Pin_1
  N7: 7_Segment_4_Digit_Display1.pin_7, ESP1.io26
  N8: 7_Segment_4_Digit_Display1.pin_8, R3.Pin_1
  N9: 7_Segment_4_Digit_Display1.pin_9, R2.Pin_1
  N10: 7_Segment_4_Digit_Display1.pin_10, ESP1.io25
  N11: 7_Segment_4_Digit_Display1.pin_11, ESP1.io23
  N12: 7_Segment_4_Digit_Display1.pin_12, R1.Pin_1
  N13: ESP1.3v3, R5.Pin_1, R6.Pin_1
  N14: ESP1.io15, R8.Pin_1
  N15: ESP1.io14, R7.Pin_1
  N16: ESP1.gnd, Q1.E, Q2.E, LED2.cathode, LED1.cathode
  N17: ESP1.io17, R1.Pin_0
  N18: ESP1.io16, R2.Pin_0
  N19: ESP1.io35, R3.Pin_0
  N20: ESP1.io34, R4.Pin_0
  N21: Q1.C, R8.Pin_0
  N22: Q2.C, R7.Pin_0
  N23: LED2.anode, R6.Pin_0
  N24: LED1.anode, R5.Pin_0

custom parts:
  7-SEGMENT-4DIGIT common anode: A 7 Segment 4 Digit common anode display, with decimal points
  Infrared LED - 5mm: A generic infrared LED (~1.2V)
